# Fritzing sketch circuit (saved by Fritzing 0.9.2b)
breadboards: 1

parts:
  Raspberry_Pi1 = Raspberry Pi 2
  L1 = Solenoid
  U1 = SPM0204UD5 [package=spm0204ud5]
  L2 = Solenoid
  L3 = Solenoid
  R1 = Photocell (LDR) [package=THT]
  C1 = Tantalum Capacitor [capacitance=1μF package="100 mil [THT, tantalum]"]
  Q1 = NPN-Transistor [package="TO92 [THT]"]
  Q2 = NPN-Transistor [package="TO92 [THT]"]
  Q3 = NPN-Transistor [package="TO92 [THT]"]
  VCC1 = Battery block 9V
  VCC2 = Battery block 9V  # not connected
  VCC3 = Battery block 9V  # not connected

nets:
  GND: Raspberry_Pi1.GND, U1.GND, C1.-, Q1.E, Q2.E, Q3.E
  N1: Raspberry_Pi1.GPIO21, Q1.B
  N2: Raspberry_Pi1.GPIO20, Q2.B
  N3: Raspberry_Pi1.GPIO16, Q3.B
  N4: Raspberry_Pi1.GPIO24, U1.GND#
  N5: Raspberry_Pi1.GPIO18, R1.pin_0, C1.+
  N6: Raspberry_Pi1.5V, U1.OUT
  N7: L1.pin2, Q2.C
  N8: L2.pin2, Q3.C
  N9: L3.pin2, Q1.C
  N10: R1.pin_1, VCC1.+

notes:
  These are three solenoid valves connected in parallel to 27 v
  3 9v battery connected in series
  This is an HC-SR04 ultrasound sensor (actual model not available in Fritzing)
  Connected to pin 23 is the trig pin of the sensor. Connect to pin 24 of Rpi is echo pinof the sensor.
